# Fritzing sketch Mapper85_DonkeyKongCountry4VRC7 (saved by Fritzing 1.0.3b)
circuit board: 9.00001cm x 5.68cm
breadboards: 1

parts:
  1-30 = Generic single row SMD female header - 30 pins [form="♀ (female)" package=THT]
  60-31 = Generic single row SMD female header - 30 pins [form="♀ (female)" package=THT]
  3_58MHz = Crystal [frequency="16 Mhz" package=SMD]
  LM358 = LM 358 Dual Op-Amp [package="DIP8 [THT]"]
  LM359 = LM 358 Dual Op-Amp [package="SO 08 [SMD]"]
  27K = Resistor [tolerance=±5% power=0.25W resistance=220 package=THT]
  2_2K = Resistor [tolerance=±5% power=0.25W resistance=220 package=THT]
  4_7nF = Ceramic Capacitor [capacitance=100nF voltage=35V package="100 mil [THT, multilayer]"]
  33K = Resistor [tolerance=±5% power=0.25W resistance=220 package=THT]
  1uF = Ceramic Capacitor [capacitance=100nF voltage=35V package="100 mil [THT, multilayer]"]
  22uF = Ceramic Capacitor [capacitance=100nF voltage=35V package="100 mil [THT, multilayer]"]
  4_3K = Resistor [tolerance=±5% power=0.25W resistance=220 package=THT]
  240K = Resistor [tolerance=±5% power=0.25W resistance=220 package=THT]
  910 = Resistor [tolerance=±5% power=0.25W resistance=220 package=THT]
  3_9K = Resistor [tolerance=±5% power=0.25W resistance=220 package=THT]
  2_2K_2 = Resistor [tolerance=±5% power=0.25W resistance=220 package=THT]
  IC3 = IC, DIP package, 32 pins [chip_label=IC]
  VRC7 = IC, DIP package, 48 pins [chip_label=IC]
  Pad1 = Pad [width=1.8450698756469115 height=2.0987357935497952 connect=center]
  Pad2 = Pad [width=1.8450698756469115 height=2.0987357935497952 connect=center]
  Pad3 = Pad [width=1.8450698756469115 height=2.0987357935497952 connect=center]
  18pf = Ceramic Capacitor [capacitance=100nF voltage=35V package="1206 [SMD, multilayer]"]
  18pf1 = Ceramic Capacitor [capacitance=100nF voltage=35V package="1206 [SMD, multilayer]"]
  IC2 = IC, DIP package, 32 pins [chip_label=IC]

nets:
  N1: 1-30.pin1, IC3.pin16
  N2: 1-30.pin2, IC3.pin25
  N3: 1-30.pin3, IC3.pin23
  N4: 1-30.pin4, IC3.pin26
  N5: 1-30.pin5, IC3.pin27
  N6: 1-30.pin6, IC3.pin5
  N7: 1-30.pin7, IC3.pin6
  N8: 1-30.pin8, VRC7.pin16
  N9: 1-30.pin9, VRC7.pin19
  N10: 1-30.pin10, IC3.pin9
  N11: 1-30.pin11, IC3.pin10
  N12: 1-30.pin12, IC3.pin11
  N13: 1-30.pin13, IC3.pin12
  N14: 1-30.pin14, VRC7.pin4
  N15: 1-30.pin15, VRC7.pin5
  N16: 1-30.pin16, LM358.connector3, LM359.connector3, 2_2K.Pin_0, 4_7nF.1, 33K.Pin_0, 1uF.0, 22uF.1, 910.Pin_1, VRC7.pin3, VRC7.pin46
  N17: 1-30.pin18, VRC7.pin6
  N18: 1-30.pin19, IC2.pin6
  N19: 1-30.pin20, IC2.pin7
  N20: 1-30.pin21, IC2.pin8
  N21: 1-30.pin22, IC2.pin9
  N22: 1-30.pin23, IC2.pin10
  N23: 1-30.pin24, IC2.pin11
  N24: 1-30.pin25, IC2.pin12
  N25: 1-30.pin30, LM358.connector4, LM358.connector5, LM358.connector7, LM359.connector4, LM359.connector5, LM359.connector7, 1uF.1, VRC7.pin42
  N26: 60-31.pin6, VRC7.pin33
  N27: 60-31.pin7, VRC7.pin32
  N28: 60-31.pin8, VRC7.pin31
  N29: 60-31.pin15, 3_9K.Pin_0, 2_2K_2.Pin_1
  N30: 60-31.pin16, 3_9K.Pin_1
  N31: 60-31.pin17, VRC7.pin45
  N32: 60-31.pin18, VRC7.pin7
  N33: 60-31.pin19, VRC7.pin8
  N34: 60-31.pin20, VRC7.pin9
  N35: 60-31.pin21, VRC7.pin10
  N36: 60-31.pin22, VRC7.pin11
  N37: 60-31.pin23, VRC7.pin12
  N38: 60-31.pin24, VRC7.pin13
  N39: 60-31.pin25, VRC7.pin14
  N40: 60-31.pin26, VRC7.pin29
  N41: 60-31.pin27, VRC7.pin28
  N42: 60-31.pin28, VRC7.pin27
  N43: 60-31.pin29, VRC7.pin47
  N44: 3_58MHz.pin_0, VRC7.pin18, Pad3.pad, 18pf1.1
  N45: 3_58MHz.pin_1, VRC7.pin17, Pad1.pad, 18pf.0
  N46: LM358.connector0, LM359.connector0, 240K.Pin_1, 910.Pin_0, 2_2K_2.Pin_0
  N47: LM358.connector1, LM359.connector1, 4_3K.Pin_0, 240K.Pin_0
  N48: LM358.connector2, LM359.connector2, 27K.Pin_0, 4_7nF.0, 33K.Pin_1
  N49: LM358.connector6, LM359.connector6
  N50: 27K.Pin_1, 2_2K.Pin_1, VRC7.pin43
  N51: 22uF.0, 4_3K.Pin_1
  N52: IC3.pin2, VRC7.pin23
  N53: IC3.pin3, VRC7.pin22
  N54: IC3.pin22, VRC7.pin44
  N55: IC3.pin28, VRC7.pin20
  N56: IC3.pin29, VRC7.pin21
  N57: IC3.pin30, VRC7.pin25
  N58: IC3.pin31, VRC7.pin26
  N59: VRC7.pin34, IC2.pin23
  N60: VRC7.pin35, IC2.pin25
  N61: VRC7.pin36, IC2.pin4
  N62: VRC7.pin37, IC2.pin28
  N63: VRC7.pin38, IC2.pin29
  N64: VRC7.pin39, IC2.pin3
  N65: VRC7.pin40, IC2.pin2
  N66: VRC7.pin41, IC2.pin30
  N67: Pad2.pad, 18pf.1, 18pf1.0

notes:
  4 VRC7 Hack Repro PCB
  Designed by HeeminYT
  If you're going to
  use oscillator,
  fi ll two capacitors above,
  if you're going to use
  use resonator instead,
  just place it on
  the three contacts on the top
  ^ the debug pin

custom parts:
  Generic single row SMD female header - 30 pins: Generic single row SMD female header
